# Fritzing sketch wifiesprx (saved by Fritzing 0.9.2b)

parts:
  Part1 = Arduino Nano (Rev3.0)
  U1 = NodeMCU V1.0
  Part3 = IMU Digital Combo Board 6DOF
  BAT1 = Battery Holders [package=lipo-1100mAh]
  BAT2 = Battery Holders [package=lipo-1100mAh]

nets:
  N1: Part1.D2, U1.D1, U1.3V3
  N2: Part1.VIN, BAT1.+
  GND: Part1.GND, U1.GND, Part3.GND, BAT2.-
  N3: Part1.A5, Part3.SCL, Part3.INT1
  N4: Part1.A4, Part3.SDA
  N5: BAT1.-, BAT2.+

notes:
  7.4 lipo battery 2s

custom parts:
  NodeMCU V1.0: ESP8266 based NodeMCU V1.0
